// Logisim project temperature.circ as structural Verilog: 1 circuit, main circuit main
// A4511
module main (
  output out_1,
  output out_2,
  output out_3
);

  wire A1_2_out, A1_3_out, A1_out, A2_2_out, A2_3_out, A2_out, A3_2_out, A3_3_out, A3_out, A4_3_out, A4_out,
       A5_out, AB_sw7, AB_sw8, B1_out, B2_2_out, B2_out, B3_2_out, B3_out, B4_2_out, B4_out, C1_out, C2_out,
       C3_out, C4_out, D1_out, D2_out, D3_out, F_2Hz_out, H_G_F_E_D_C_B_A_2_sw5, H_G_F_E_D_C_B_A_2_sw6,
       H_G_F_E_D_C_B_A_2_sw7, H_G_F_E_D_C_B_A_2_sw8, H_G_F_E_D_C_B_A_sw1, H_G_F_E_D_C_B_A_sw2,
       H_G_F_E_D_C_B_A_sw3, H_G_F_E_D_C_B_A_sw4, H_G_F_E_D_C_B_A_sw5, H_G_F_E_D_C_B_A_sw6,
       H_G_F_E_D_C_B_A_sw7, H_G_F_E_D_C_B_A_sw8, main_1_p5, main_1_p6, main_1_p7, main_1_p8, main_1_p9,
       main_1_p10, main_1_p11;

  DipSwitch H_G_F_E_D_C_B_A (
    .sw1(H_G_F_E_D_C_B_A_sw1), .sw2(H_G_F_E_D_C_B_A_sw2), .sw3(H_G_F_E_D_C_B_A_sw3),
    .sw4(H_G_F_E_D_C_B_A_sw4), .sw5(H_G_F_E_D_C_B_A_sw5), .sw6(H_G_F_E_D_C_B_A_sw6),
    .sw7(H_G_F_E_D_C_B_A_sw7), .sw8(H_G_F_E_D_C_B_A_sw8));
  DipSwitch AB (.sw7(AB_sw7), .sw8(AB_sw8));  // open: sw1, sw2, sw3, sw4, sw5, sw6
  DipSwitch H_G_F_E_D_C_B_A_2 (
    .sw5(H_G_F_E_D_C_B_A_2_sw5), .sw6(H_G_F_E_D_C_B_A_2_sw6), .sw7(H_G_F_E_D_C_B_A_2_sw7),
    .sw8(H_G_F_E_D_C_B_A_2_sw8));  // open: sw1, sw2, sw3, sw4
  or A1 (A1_out, H_G_F_E_D_C_B_A_sw5, H_G_F_E_D_C_B_A_sw6);
  or A2 (A2_out, H_G_F_E_D_C_B_A_sw7, H_G_F_E_D_C_B_A_sw8);
  not A1_2 (A1_2_out, H_G_F_E_D_C_B_A_sw1);
  and A3 (A3_out, A1_2_out, A2_2_out);
  not A2_2 (A2_2_out, H_G_F_E_D_C_B_A_sw2);
  not A3_2 (A3_2_out, H_G_F_E_D_C_B_A_sw3);
  not A4 (A4_out, AB_sw7);
  not A5 (A5_out, AB_sw8);
  and B1 (B1_out, H_G_F_E_D_C_B_A_2_sw7, H_G_F_E_D_C_B_A_2_sw8);
  or A3_3 (A3_3_out, A1_out, A2_out);
  and A4_2 (out_2, A3_out, A3_2_out);
  and B2 (B2_out, H_G_F_E_D_C_B_A_2_sw6, B1_out);
  and A1_3 (A1_3_out, H_G_F_E_D_C_B_A_sw4, A3_3_out);
  and C2 (C2_out, AB_sw7, A5_out);
  and C1 (C1_out, AB_sw7, AB_sw8);
  and B3 (B3_out, H_G_F_E_D_C_B_A_2_sw5, B2_out);
  not A6 (out_3, B3_out);
  or A4_3 (A4_3_out, H_G_F_E_D_C_B_A_sw3, A1_3_out);
  and D2 (D2_out, AB_sw8, A4_out);
  and D1 (D1_out, out_2, C2_out);
  and C3 (C3_out, A4_out, A5_out);
  and B4 (B4_out, C1_out, out_3);
  Clock F_2Hz (.out(F_2Hz_out));
  and A2_3 (A2_3_out, H_G_F_E_D_C_B_A_sw2, A4_3_out);
  and D3 (D3_out, out_1, D2_out);
  or B1_2 (out_1, H_G_F_E_D_C_B_A_sw1, A2_3_out);
  and C4 (C4_out, C3_out, F_2Hz_out);
  or B2_2 (B2_2_out, D1_out, B4_out);
  // _4511_main main_1: pin names not known; wires that end beside it: 1'b0, 1'b0, AB_sw7, AB_sw8, main_1_p5, main_1_p6, main_1_p7, main_1_p8, main_1_p9, main_1_p10, main_1_p11
  or B3_2 (B3_2_out, D3_out, B2_2_out);
  _7_Segment_Display u_7_segment_display_1 (
    .g(main_1_p5), .f(main_1_p7), .a(main_1_p9), .b(main_1_p11), .e(main_1_p6), .d(main_1_p8),
    .c(main_1_p10), .dp(B4_2_out));
  or B4_2 (B4_2_out, C4_out, B3_2_out);
endmodule
